# Fritzing sketch DS1621 (saved by Fritzing 0.9.3b)
breadboards: 1

parts:
  IC1 = IC, DIP package, 8 pins [chip_label=DS1621]
  FR1 = Franzininho
  R1 = Resistor [tolerance=±5% resistance=4.7k package=THT]  # not connected
  R2 = Resistor [tolerance=±5% resistance=4.7k package=THT]

nets:
  N1: IC1.pin1, FR1.P0
  N2: IC1.pin2, FR1.P2, R2.Pin_1
  N3: IC1.pin4, IC1.pin5, IC1.pin6, IC1.pin7, FR1.GND
  N4: IC1.pin8, FR1.VCC, R2.Pin_0

custom parts:
  Franzininho: A Franzininho é uma placa com ATtiny85 compatível com o Arduino Gemma. Ela foi desenvolvida com objetivo de promover a inclusão no mundo da eletrônica e programação. O circuito em face simples e com componentes PTHs, facilita o uso da placa em oficinas de solda. Por ser compatível com a plataforma Arduino, pode ela também pode ser usada para atividades de programação tanto para iniciantes como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
