# Fritzing sketch circuitoFritzing (saved by Fritzing 0.9.3b)
breadboards: 1

parts:
  FR1 = Franzininho
  S1 = Pushbutton [package="[THT]"]

nets:
  N1: FR1.GND, S1.Pin_3, S1.Pin_4
  N2: FR1.P2, S1.Pin_1, S1.Pin_2

custom parts:
  Franzininho: A Franzininho é uma placa com ATtiny85 compatível com o Arduino Gemma. Ela foi desenvolvida com objetivo de promover a inclusão no mundo da eletrônica e programação. O circuito em face simples e com componentes PTHs, facilita o uso da placa em oficinas de solda. Por ser compatível com a plataforma Arduino, pode ela também pode ser usada para atividades de programação tanto para iniciantes como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
