# Fritzing sketch semaforo (saved by Fritzing 0.9.3b)
breadboards: 1

parts:
  FR1 = Franzininho
  LED1 = LED - 5mm [color="Red (633nm)" package="5 mm [THT]"]
  LED2 = LED - 5mm [color="Yellow (595nm)" package="5 mm [THT]"]
  LED3 = LED - 5mm [color="Green (570nm)" package="5 mm [THT]"]
  R1 = Resistor [tolerance=±5% resistance=330 package=THT]
  R2 = Resistor [tolerance=±5% resistance=330 package=THT]
  R3 = Resistor [tolerance=±5% resistance=330 package=THT]

nets:
  N1: FR1.GND, LED1.cathode, LED2.cathode, LED3.cathode
  N2: FR1.P2, R1.Pin_0
  N3: FR1.P1, R2.Pin_0
  N4: FR1.P0, R3.Pin_0
  N5: LED1.anode, R1.Pin_1
  N6: LED2.anode, R2.Pin_1
  N7: LED3.anode, R3.Pin_1

custom parts:
  Franzininho: A Franzininho é uma placa com ATtiny85 compatível com o Arduino Gemma. Ela foi desenvolvida com objetivo de promover a inclusão no mundo da eletrônica e programação. O circuito em face simples e com componentes PTHs, facilita o uso da placa em oficinas de solda. Por ser compatível com a plataforma Arduino, pode ela também pode ser usada para atividades de programação tanto para iniciantes como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
