# Fritzing sketch circuitoLDR (saved by Fritzing 0.9.2b)
breadboards: 1

parts:
  FR1 = Franzininho
  R1 = Resistor [tolerance=±5% resistance=330 package=THT]
  LED1 = LED - 5mm [color="Red (633nm)" package="5 mm [THT]"]
  R2 = Photocell (LDR) [package=THT]
  R3 = Resistor [tolerance=±5% resistance=10k package=THT]

nets:
  N1: FR1.GND, LED1.cathode, R2.pin_1
  N2: FR1.VCC, R3.Pin_0
  N3: FR1.P2, R2.pin_0, R3.Pin_1
  N4: FR1.P1, R1.Pin_0
  N5: R1.Pin_1, LED1.anode

custom parts:
  Franzininho: A Franzininho é uma placa com ATtiny85 compatível com o Arduino Gemma. Ela foi desenvolvida com objetivo de promover a inclusão no mundo da eletrônica e programação. O circuito em face simples e com componentes PTHs, facilita o uso da placa em oficinas de solda. Por ser compatível com a plataforma Arduino, pode ela também pode ser usada para atividades de programação tanto para iniciantes como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
